# Fritzing sketch blaster (saved by Fritzing 0.9.3b)
circuit board: 1.5cm x 2.3cm
breadboards: 1

parts:
  R1 = Resistor [tolerance=±5% resistance=10k package=THT]
  R2 = Resistor [tolerance=±5% resistance=330 package=THT]
  U1 = attiny85 [package=dip]
  VCC1 = Battery
  J1 = female pin header, 2 pins [form="♀ (female)"]
  J2 = female pin header, 2 pins [form="♀ (female)"]
  J3 = female pin header, 2 pins [form="♀ (female)"]

nets:
  N1: R1.Pin_0, U1.Pin_4, VCC1.-, J2.pin2
  N2: R1.Pin_1, U1.Pin_5, J3.pin1
  N3: R2.Pin_0, J1.pin2, J2.pin1
  N4: R2.Pin_1, U1.Pin_6
  N5: U1.Pin_8, VCC1.+, J1.pin1, J3.pin2
